# Fritzing sketch SBMInfo (saved by Fritzing 0.9.4)
breadboards: 1

parts:
  Arduino_Nano = Arduino Nano (Rev3.0)
  R9 = Resistor [tolerance=±5% resistance=1k package=THT]
  R12 = Trimmer Potentiometer [maximum_resistance=10kΩ package=THT]
  1% = Resistor [tolerance=±1% resistance=100k package=THT]
  1%_2 = Resistor [tolerance=±1% resistance=22k package=THT]
  R13 = Resistor [tolerance=±5% resistance=1k package=THT]
  LCD1 = 20x4 LCD display [part_number=2004A]
  1%_3 = Resistor [tolerance=±1% resistance=100k package=THT]
  1%_4 = Resistor [tolerance=±1% resistance=10k package=THT]

nets:
  N1: Arduino_Nano.D3, LCD1.DB4
  N2: Arduino_Nano.D4, LCD1.DB5
  N3: Arduino_Nano.D5, LCD1.DB6
  N4: Arduino_Nano.D6, LCD1.DB7
  N5: Arduino_Nano.D7, LCD1.RS
  N6: Arduino_Nano.D8, LCD1.E
  5V: Arduino_Nano.5V, R12.leg1, LCD1.Vdd, LCD1.A_+
  N7: Arduino_Nano.A5, R13.Pin_0
  N8: Arduino_Nano.A4, R9.Pin_0
  N9: Arduino_Nano.A3, 1%_4.Pin_0
  N10: Arduino_Nano.A2, 1%_2.Pin_1
  N11: Arduino_Nano.A1, 1%_3.Pin_0
  N12: Arduino_Nano.A0, 1%.Pin_0, 1%_2.Pin_0
  N13: R12.wiper, LCD1.Vo
  N14: R12.leg2, LCD1.Vss, LCD1.R/W, LCD1.K_-
  N15: 1%.Pin_1, 1%_3.Pin_1, 1%_4.Pin_1

custom parts:
  20x4 LCD display: 20x4 character display. CHECK LED POLARITY BEFORE CONNECTING POWER Some versions of the dispaly have the polarity of the LED pins "A" and "K" reversed.
